// Logisim project logisim_circuit_diagram.circ as structural Verilog: 1 circuit, main circuit main
module main (
  input  [7:0] in_1,
  input  [7:0] in_2,
  input  [7:0] in_3,
  input  [7:0] in_4,
  input  [7:0] in_5,
  input  in_6,
  input  in_7,
  input  [7:0] in_8,
  input  [7:0] in_9,
  input  in_10,
  input  [7:0] in_11,
  input  [7:0] in_12,
  input  [7:0] in_13,
  input  in_14,
  input  [3:0] in_15,
  input  [7:0] in_16,
  input  [3:0] _0,
  input  [7:0] in_18,
  input  [3:0] _1,
  input  [7:0] in_20,
  input  [3:0] _5,
  input  [7:0] in_22,
  input  [3:0] _2,
  input  [7:0] in_24,
  input  [3:0] _10,
  input  [3:0] _3,
  input  [3:0] _15,
  input  [7:0] in_28,
  input  [7:0] in_29,
  input  [7:0] in_30,
  input  [7:0] in_31,
  input  [7:0] in_32,
  input  [7:0] in_33,
  input  [7:0] in_34,
  input  [7:0] in_35,
  input  [7:0] in_36,
  input  [7:0] in_37,
  input  [7:0] in_38,
  input  [7:0] in_39,
  input  [7:0] in_40,
  input  [7:0] in_41,
  input  [7:0] in_42,
  input  [7:0] in_43,
  input  [7:0] in_44,
  input  [7:0] in_45,
  input  [7:0] in_46,
  input  [7:0] in_47,
  input  [7:0] in_48,
  input  [7:0] in_49,
  input  [7:0] in_50,
  input  [7:0] in_51,
  input  [7:0] in_52,
  input  [7:0] in_53,
  input  [7:0] in_54,
  input  [3:0] _0_2,
  input  [3:0] _1_2,
  input  [3:0] _5_2,
  input  [3:0] _2_2,
  input  [3:0] _10_2,
  input  [7:0] in_60,
  input  [3:0] _3_2,
  input  [7:0] in_62,
  input  [3:0] _15_2,
  input  [7:0] in_64,
  input  [7:0] in_65,
  input  [7:0] in_66,
  input  [7:0] in_67,
  input  [7:0] in_68,
  input  [7:0] in_69,
  input  [7:0] in_70,
  input  [7:0] in_71,
  output [1:0] out_72,
  output [3:0] out_73,
  output [3:0] out_74,
  output [3:0] out_75,
  output out_76,
  output [3:0] out_77,
  output [3:0] out_78,
  output out_79,
  output [1:0] out_80,
  output [3:0] out_81,
  output [3:0] out_82,
  output out_83,
  output [3:0] out_84,
  output [3:0] out_85,
  output out_86,
  output [1:0] out_87,
  output [1:0] out_88,
  output [3:0] out_89,
  output [1:0] out_90,
  output [1:0] out_91,
  output [1:0] out_92,
  output [1:0] out_93,
  output [1:0] out_94,
  output [1:0] out_95
);

  wire _0_out, _1_2_out, _1_3_out, _1_4_out, _1_5_out, _1_6_out, _1_out, _2_2_out, _2_3_out, _2_4_out,
       _2_5_out, _2_6_out, _2_out, _3_2_out, _3_3_out, _3_4_out, _3_5_out, _3_6_out, _3_out, and_1_out,
       and_2_out, and_3_out, and_4_out, and_5_out, and_6_out, and_7_out, and_8_out, and_9_out, and_10_out,
       and_11_out, and_12_out, and_13_out, and_14_out, and_15_out, and_16_out, and_17_out, and_18_out,
       and_19_out, and_20_out, and_21_out, and_22_out, and_23_out, and_24_out, and_25_out, and_26_out,
       and_27_out, and_28_out, and_29_out, and_30_out, and_31_out, and_32_out, and_33_out, and_34_out,
       and_35_out, and_36_out, and_37_out, and_38_out, and_39_out, and_40_out, and_41_out, and_42_out,
       and_43_out, and_44_out, and_45_out, and_46_out, and_47_out, and_48_out, and_49_out, comparator_1_eq,
       comparator_1_gt, comparator_1_lt, comparator_2_eq, comparator_2_lt, comparator_3_eq, comparator_3_gt,
       comparator_4_eq, comparator_4_gt, comparator_4_lt, comparator_5_eq, comparator_5_gt, comparator_5_lt,
       comparator_6_eq, comparator_6_lt, comparator_7_eq, comparator_7_gt, comparator_8_eq, comparator_8_gt,
       comparator_8_lt, comparator_9_eq, comparator_9_gt, comparator_9_lt, comparator_10_eq,
       comparator_10_lt, comparator_11_eq, comparator_11_gt, comparator_12_eq, comparator_12_gt,
       comparator_12_lt, comparator_13_eq, comparator_13_gt, comparator_13_lt, comparator_14_eq,
       comparator_14_lt, comparator_15_eq, comparator_15_gt, comparator_16_eq, comparator_16_gt,
       comparator_16_lt, comparator_17_eq, comparator_17_gt, comparator_17_lt, comparator_18_eq,
       comparator_18_lt, comparator_19_eq, comparator_19_gt, comparator_20_eq, comparator_20_gt,
       comparator_20_lt, comparator_21_eq, comparator_21_gt, comparator_21_lt, comparator_22_eq,
       comparator_22_lt, comparator_23_eq, comparator_23_gt, comparator_24_eq, comparator_24_gt,
       comparator_24_lt, comparator_25_eq, comparator_25_gt, comparator_25_lt, comparator_26_eq,
       comparator_26_lt, comparator_27_eq, comparator_27_gt, comparator_28_eq, comparator_28_lt,
       comparator_29_eq, comparator_29_gt, comparator_30_eq, comparator_30_gt, comparator_30_lt,
       comparator_31_eq, comparator_31_gt, comparator_31_lt, comparator_32_eq, comparator_32_lt,
       comparator_33_eq, comparator_33_gt, comparator_34_eq, comparator_34_gt, comparator_34_lt,
       comparator_35_lt, comparator_36_lt, comparator_37_lt, comparator_38_lt, comparator_39_eq,
       comparator_39_gt, comparator_39_lt, comparator_40_eq, comparator_40_lt, comparator_41_eq,
       comparator_41_gt, comparator_42_eq, comparator_42_gt, comparator_42_lt, comparator_43_eq,
       comparator_44_eq, comparator_44_gt, comparator_45_eq, comparator_45_lt, comparator_46_eq,
       comparator_46_gt, comparator_47_eq, comparator_47_lt, comparator_48_eq, comparator_48_gt,
       comparator_49_eq, comparator_49_lt, comparator_50_eq, comparator_51_eq, comparator_51_gt,
       comparator_52_eq, comparator_52_lt, comparator_53_eq, comparator_53_gt, comparator_54_eq,
       comparator_54_lt, comparator_55_eq, comparator_55_gt, comparator_56_eq, comparator_56_lt, or_1_out,
       or_2_out, or_3_out, or_4_out, or_5_out, or_6_out, or_7_out, or_8_out, or_9_out, or_10_out, or_11_out,
       or_12_out, or_13_out, or_14_out, or_15_out, or_16_out, or_17_out, or_18_out, or_19_out, or_20_out,
       or_21_out, or_22_out, or_23_out, or_24_out, or_25_out, or_26_out, or_27_out;
  wire [3:0] adder_2_out, adder_5_out, bit_extender_4_out, bit_extender_5_out, bit_extender_7_out;

  Comparator #(.mode("unsigned")) comparator_1 (
    .a(in_1), .b(in_2), .gt(comparator_1_gt), .eq(comparator_1_eq), .lt(comparator_1_lt));
  Comparator comparator_2 (.a(in_1), .b(in_3), .eq(comparator_2_eq), .lt(comparator_2_lt));  // open: gt
  Comparator comparator_3 (.a(in_1), .b(in_4), .gt(comparator_3_gt), .eq(comparator_3_eq));  // open: lt
  Comparator #(.mode("unsigned")) comparator_4 (
    .a(in_1), .b(in_5), .gt(comparator_4_gt), .eq(comparator_4_eq), .lt(comparator_4_lt));
  and and_1 (and_1_out, comparator_1_gt, comparator_2_lt);
  and and_2 (and_2_out, comparator_3_gt, comparator_4_lt);
  or or_1 (or_1_out, and_2_out, comparator_3_eq, comparator_4_eq);
  Comparator comparator_5 (.a(in_28), .b(in_30), .gt(comparator_5_gt), .eq(comparator_5_eq), .lt(comparator_5_lt));
  Comparator comparator_6 (.a(in_28), .b(in_32), .eq(comparator_6_eq), .lt(comparator_6_lt));  // open: gt
  Comparator comparator_7 (.a(in_28), .b(in_34), .gt(comparator_7_gt), .eq(comparator_7_eq));  // open: lt
  Comparator comparator_8 (.a(in_28), .b(in_36), .gt(comparator_8_gt), .eq(comparator_8_eq), .lt(comparator_8_lt));
  or or_2 (or_2_out, and_1_out, comparator_1_eq, comparator_2_eq);
  Comparator #(.mode("unsigned")) comparator_9 (
    .a(in_8), .b(in_9), .gt(comparator_9_gt), .eq(comparator_9_eq), .lt(comparator_9_lt));
  Comparator #(.mode("unsigned")) comparator_10 (
    .a(in_8), .b(in_11), .eq(comparator_10_eq), .lt(comparator_10_lt));  // open: gt
  Comparator #(.mode("unsigned")) comparator_11 (
    .a(in_8), .b(in_12), .gt(comparator_11_gt), .eq(comparator_11_eq));  // open: lt
  Comparator #(.mode("unsigned")) comparator_12 (
    .a(in_8), .b(in_13), .gt(comparator_12_gt), .eq(comparator_12_eq), .lt(comparator_12_lt));
  and and_3 (and_3_out, comparator_7_gt, comparator_8_lt);
  Comparator #(.mode("unsigned")) comparator_13 (
    .a(in_45), .b(in_46), .gt(comparator_13_gt), .eq(comparator_13_eq), .lt(comparator_13_lt));
  Comparator #(.mode("unsigned")) comparator_14 (
    .a(in_45), .b(in_47), .eq(comparator_14_eq), .lt(comparator_14_lt));  // open: gt
  Comparator #(.mode("unsigned")) comparator_15 (
    .a(in_45), .b(in_48), .gt(comparator_15_gt), .eq(comparator_15_eq));  // open: lt
  Comparator #(.mode("unsigned")) comparator_16 (
    .a(in_45), .b(in_49), .gt(comparator_16_gt), .eq(comparator_16_eq), .lt(comparator_16_lt));
  Comparator #(.mode("unsigned")) comparator_17 (
    .a(in_50), .b(in_51), .gt(comparator_17_gt), .eq(comparator_17_eq), .lt(comparator_17_lt));
  Comparator #(.mode("unsigned")) comparator_18 (
    .a(in_50), .b(in_52), .eq(comparator_18_eq), .lt(comparator_18_lt));  // open: gt
  Comparator #(.mode("unsigned")) comparator_19 (
    .a(in_50), .b(in_53), .gt(comparator_19_gt), .eq(comparator_19_eq));  // open: lt
  Comparator #(.mode("unsigned")) comparator_20 (
    .a(in_50), .b(in_54), .gt(comparator_20_gt), .eq(comparator_20_eq), .lt(comparator_20_lt));
  and and_4 (and_4_out, comparator_9_gt, comparator_10_lt);
  and and_5 (and_5_out, comparator_11_gt, comparator_12_lt);
  Comparator comparator_21 (.a(in_16), .b(in_18), .gt(comparator_21_gt), .eq(comparator_21_eq), .lt(comparator_21_lt));
  Comparator comparator_22 (.a(in_16), .b(in_20), .eq(comparator_22_eq), .lt(comparator_22_lt));  // open: gt
  Comparator comparator_23 (.a(in_16), .b(in_22), .gt(comparator_23_gt), .eq(comparator_23_eq));  // open: lt
  Comparator comparator_24 (.a(in_16), .b(in_24), .gt(comparator_24_gt), .eq(comparator_24_eq), .lt(comparator_24_lt));
  and and_6 (and_6_out, comparator_5_gt, comparator_6_lt);
  or or_3 (or_3_out, and_3_out, comparator_7_eq, comparator_8_eq);
  and and_7 (and_7_out, comparator_15_gt, comparator_16_lt);
  and and_8 (and_8_out, comparator_19_gt, comparator_20_lt);
  Priority_Encoder #(.select(2)) priority_encoder_1 (
    .in0(or_2_out), .in1(or_1_out), .in2(comparator_4_gt), .in3(comparator_1_lt), .out(out_72));  // open: gs, en_out, en_in
  or or_4 (or_4_out, and_5_out, comparator_11_eq, comparator_12_eq);
  or or_5 (or_5_out, and_6_out, comparator_5_eq, comparator_6_eq);
  and and_9 (and_9_out, comparator_13_gt, comparator_14_lt);
  and and_10 (and_10_out, comparator_17_gt, comparator_18_lt);
  or or_6 (or_6_out, and_4_out, comparator_9_eq, comparator_10_eq);
  and and_11 (and_11_out, comparator_23_gt, comparator_24_lt);
  or or_7 (or_7_out, and_7_out, comparator_15_eq, comparator_16_eq);
  or or_8 (or_8_out, and_8_out, comparator_19_eq, comparator_20_eq);
  and and_12 (and_12_out, comparator_21_gt, comparator_22_lt);
  or or_9 (or_9_out, and_11_out, comparator_23_eq, comparator_24_eq);
  Comparator comparator_25 (.a(in_38), .b(in_39), .gt(comparator_25_gt), .eq(comparator_25_eq), .lt(comparator_25_lt));
  Comparator comparator_26 (.a(in_38), .b(in_40), .eq(comparator_26_eq), .lt(comparator_26_lt));  // open: gt
  Comparator comparator_27 (.a(in_38), .b(in_41), .gt(comparator_27_gt), .eq(comparator_27_eq));  // open: lt
  Comparator comparator_28 (.a(in_38), .b(in_42), .eq(comparator_28_eq), .lt(comparator_28_lt));  // open: gt
  Comparator comparator_29 (.a(in_38), .b(in_43), .gt(comparator_29_gt), .eq(comparator_29_eq));  // open: lt
  Comparator comparator_30 (.a(in_38), .b(in_44), .gt(comparator_30_gt), .eq(comparator_30_eq), .lt(comparator_30_lt));
  or or_10 (or_10_out, and_9_out, comparator_13_eq, comparator_14_eq);
  or or_11 (or_11_out, and_10_out, comparator_17_eq, comparator_18_eq);
  or or_12 (or_12_out, and_12_out, comparator_21_eq, comparator_22_eq);
  or or_13 (or_13_out, comparator_26_eq, comparator_26_lt);
  and and_13 (and_13_out, comparator_29_gt, comparator_30_lt);
  Comparator comparator_31 (.a(in_60), .b(in_62), .gt(comparator_31_gt), .eq(comparator_31_eq), .lt(comparator_31_lt));
  Comparator comparator_32 (.a(in_60), .b(in_64), .eq(comparator_32_eq), .lt(comparator_32_lt));  // open: gt
  Comparator comparator_33 (.a(in_60), .b(in_65), .gt(comparator_33_gt), .eq(comparator_33_eq));  // open: lt
  Comparator comparator_34 (.a(in_60), .b(in_66), .gt(comparator_34_gt), .eq(comparator_34_eq), .lt(comparator_34_lt));
  Priority_Encoder #(.select(2)) priority_encoder_2 (
    .in0(or_6_out), .in1(or_4_out), .in2(comparator_12_gt), .in3(comparator_9_lt), .out(out_80));  // open: gs, en_out, en_in
  and and_14 (and_14_out, comparator_27_gt, comparator_28_lt);
  or or_14 (or_14_out, and_13_out, comparator_29_eq, comparator_30_eq);
  and and_15 (and_15_out, comparator_33_gt, comparator_34_lt);
  and and_16 (and_16_out, comparator_31_gt, comparator_32_lt);
  assign out_73 = {{2{1'b0}}, out_72};  // Bit_Extender bit_extender_1
  assign out_75 = {{2{1'b0}}, out_80};  // Bit_Extender bit_extender_2
  Priority_Encoder #(.select(2)) priority_encoder_3 (
    .in0(or_9_out), .in1(or_12_out), .in2(comparator_24_gt), .in3(comparator_21_lt), .out(out_87));  // open: gs, en_out, en_in
  or or_15 (or_15_out, comparator_13_lt, comparator_17_lt);
  or or_16 (or_16_out, or_10_out, or_11_out);
  or or_17 (or_17_out, or_7_out, or_8_out);
  or or_18 (or_18_out, comparator_16_gt, comparator_20_gt);
  or or_19 (or_19_out, and_15_out, comparator_33_eq, comparator_34_eq);
  and and_17 (and_17_out, comparator_25_gt, or_13_out);
  or or_20 (or_20_out, and_14_out, comparator_27_eq, comparator_28_eq);
  or or_21 (or_21_out, and_16_out, comparator_31_eq, comparator_32_eq);
  Comparator #(.mode("unsigned")) comparator_35 (.a(in_29), .b(in_31), .lt(comparator_35_lt));  // open: gt, eq
  Comparator #(.mode("unsigned")) comparator_36 (.a(in_29), .b(in_33), .lt(comparator_36_lt));  // open: gt, eq
  Comparator #(.mode("unsigned")) comparator_37 (.a(in_29), .b(in_35), .lt(comparator_37_lt));  // open: gt, eq
  Comparator #(.mode("unsigned")) comparator_38 (.a(in_29), .b(in_37), .lt(comparator_38_lt));  // open: gt, eq
  Adder #(.width(4)) adder_1 (.a(out_73), .b(out_75), .out(out_74), .cin(in_6), .cout(out_76));
  or or_22 (or_22_out, comparator_25_lt, comparator_25_eq);
  Priority_Encoder #(.select(2)) priority_encoder_4 (
    .in0(or_18_out), .in1(or_17_out), .in2(or_16_out), .in3(or_15_out), .out(out_92));  // open: gs, en_out, en_in
  and and_18 (and_18_out, comparator_5_lt, comparator_35_lt);
  and and_19 (and_19_out, or_5_out, comparator_36_lt);
  and and_20 (and_20_out, or_3_out, comparator_37_lt);
  and and_21 (and_21_out, comparator_38_lt, comparator_8_gt);
  Priority_Encoder #(.select(2)) priority_encoder_5 (
    .in0(comparator_31_lt), .in1(or_21_out), .in2(or_19_out), .in3(comparator_34_gt), .out(out_94));  // open: gs, en_out, en_in
  Comparator #(.mode("unsigned")) comparator_39 (
    .a(in_67), .b(in_68), .gt(comparator_39_gt), .eq(comparator_39_eq), .lt(comparator_39_lt));
  Comparator #(.mode("unsigned")) comparator_40 (
    .a(in_67), .b(in_69), .eq(comparator_40_eq), .lt(comparator_40_lt));  // open: gt
  Comparator #(.mode("unsigned")) comparator_41 (
    .a(in_67), .b(in_70), .gt(comparator_41_gt), .eq(comparator_41_eq));  // open: lt
  Comparator #(.mode("unsigned")) comparator_42 (
    .a(in_67), .b(in_71), .gt(comparator_42_gt), .eq(comparator_42_eq), .lt(comparator_42_lt));
  and and_22 (and_22_out, comparator_41_gt, comparator_42_lt);
  assign out_78 = {{2{1'b0}}, out_87};  // Bit_Extender bit_extender_3
  and and_23 (and_23_out, comparator_39_gt, comparator_40_lt);
  or or_23 (or_23_out, and_22_out, comparator_41_eq, comparator_42_eq);
  Priority_Encoder #(.select(2)) priority_encoder_6 (
    .in0(and_18_out), .in1(and_19_out), .in2(and_20_out), .in3(and_21_out), .out(out_90));  // open: gs, en_out, en_in
  assign bit_extender_4_out = {{2{1'b0}}, out_92};  // Bit_Extender bit_extender_4
  assign bit_extender_5_out = {{2{1'b0}}, out_94};  // Bit_Extender bit_extender_5
  Adder #(.width(4)) adder_2 (.a(bit_extender_4_out), .b(bit_extender_5_out), .out(adder_2_out));  // open: cin, cout
  or or_24 (or_24_out, and_23_out, comparator_39_eq, comparator_40_eq);
  Adder #(.width(4)) adder_3 (.a(out_74), .b(out_78), .out(out_77), .cin(in_7), .cout(out_79));
  assign out_82 = {{2{1'b0}}, out_90};  // Bit_Extender bit_extender_6
  and and_24 (and_24_out, comparator_5_lt, or_22_out);
  and and_25 (and_25_out, or_5_out, or_22_out);
  and and_26 (and_26_out, or_3_out, or_22_out);
  and and_27 (and_27_out, comparator_8_gt, or_22_out);
  and and_28 (and_28_out, comparator_5_lt, and_17_out);
  and and_29 (and_29_out, or_5_out, and_17_out);
  and and_30 (and_30_out, or_3_out, and_17_out);
  and and_31 (and_31_out, comparator_8_gt, and_17_out);
  and and_32 (and_32_out, comparator_5_lt, or_20_out);
  and and_33 (and_33_out, or_5_out, or_20_out);
  and and_34 (and_34_out, or_3_out, or_20_out);
  and and_35 (and_35_out, comparator_8_gt, or_20_out);
  and and_36 (and_36_out, comparator_5_lt, or_14_out);
  and and_37 (and_37_out, or_5_out, or_14_out);
  and and_38 (and_38_out, or_3_out, or_14_out);
  and and_39 (and_39_out, comparator_8_gt, or_14_out);
  and and_40 (and_40_out, or_3_out, comparator_30_gt);
  and and_41 (and_41_out, comparator_8_gt, comparator_30_gt);
  and and_42 (and_42_out, comparator_5_lt, comparator_30_gt);
  and and_43 (and_43_out, or_5_out, comparator_30_gt);
  Priority_Encoder #(.select(2)) priority_encoder_7 (
    .in0(comparator_39_lt), .in1(or_24_out), .in2(or_23_out), .in3(comparator_42_gt), .out(out_95));  // open: gs, en_out, en_in
  or u__1 (_1_out, or_24_out, or_18_out, or_21_out);
  or u__2 (_2_out, or_17_out, or_19_out, or_23_out);
  or u__3 (_3_out, comparator_42_gt, comparator_34_gt, or_15_out);
  Adder #(.width(4)) adder_4 (.a(out_77), .b(out_82), .out(out_81), .cin(in_10), .cout(out_83));
  assign bit_extender_7_out = {{2{1'b0}}, out_95};  // Bit_Extender bit_extender_7
  Adder #(.width(4)) adder_5 (.a(adder_2_out), .b(bit_extender_7_out), .out(adder_5_out));  // open: cin, cout
  assign out_85 = {{2{1'b0}}, out_91};  // Bit_Extender bit_extender_8
  or u__0 (_0_out, and_24_out, and_25_out, and_26_out, and_27_out, and_28_out, and_32_out, and_36_out);
  or or_25 (or_25_out, and_29_out, and_33_out, and_37_out, and_42_out);
  or or_26 (or_26_out, and_34_out, and_43_out, and_30_out);
  or or_27 (or_27_out, and_38_out, and_31_out, and_39_out, and_40_out, and_41_out, and_35_out);
  Adder #(.width(4)) adder_6 (.a(out_81), .b(out_85), .out(out_84), .cin(in_14), .cout(out_86));
  Priority_Encoder #(.select(2)) priority_encoder_8 (
    .in0(_0_out), .in1(or_25_out), .in2(or_26_out), .in3(or_27_out), .out(out_91));  // open: gs, en_out, en_in
  Comparator #(.width(4), .mode("unsigned")) comparator_43 (.a(in_15), .b(_0), .eq(comparator_43_eq));  // open: gt, lt
  Comparator #(.width(4), .mode("unsigned")) comparator_44 (
    .a(in_15), .b(_1), .gt(comparator_44_gt), .eq(comparator_44_eq));  // open: lt
  Comparator #(.width(4), .mode("unsigned")) comparator_45 (
    .a(in_15), .b(_5), .eq(comparator_45_eq), .lt(comparator_45_lt));  // open: gt
  Comparator #(.width(4), .mode("unsigned")) comparator_46 (
    .a(in_15), .b(_2), .gt(comparator_46_gt), .eq(comparator_46_eq));  // open: lt
  Comparator #(.width(4), .mode("unsigned")) comparator_47 (
    .a(in_15), .b(_10), .eq(comparator_47_eq), .lt(comparator_47_lt));  // open: gt
  Comparator #(.width(4), .mode("unsigned")) comparator_48 (
    .a(in_15), .b(_3), .gt(comparator_48_gt), .eq(comparator_48_eq));  // open: lt
  Comparator #(.width(4), .mode("unsigned")) comparator_49 (
    .a(in_15), .b(_15), .eq(comparator_49_eq), .lt(comparator_49_lt));  // open: gt
  Comparator #(.width(4), .mode("unsigned")) comparator_50 (
    .a(adder_5_out), .b(_0_2), .eq(comparator_50_eq));  // open: gt, lt
  Comparator #(.width(4), .mode("unsigned")) comparator_51 (
    .a(adder_5_out), .b(_1_2), .gt(comparator_51_gt), .eq(comparator_51_eq));  // open: lt
  Comparator #(.width(4), .mode("unsigned")) comparator_52 (
    .a(adder_5_out), .b(_5_2), .eq(comparator_52_eq), .lt(comparator_52_lt));  // open: gt
  Comparator #(.width(4), .mode("unsigned")) comparator_53 (
    .a(adder_5_out), .b(_2_2), .gt(comparator_53_gt), .eq(comparator_53_eq));  // open: lt
  Comparator #(.width(4), .mode("unsigned")) comparator_54 (
    .a(adder_5_out), .b(_10_2), .eq(comparator_54_eq), .lt(comparator_54_lt));  // open: gt
  Comparator #(.width(4), .mode("unsigned")) comparator_55 (
    .a(adder_5_out), .b(_3_2), .gt(comparator_55_gt), .eq(comparator_55_eq));  // open: lt
  Comparator #(.width(4), .mode("unsigned")) comparator_56 (
    .a(adder_5_out), .b(_15_2), .eq(comparator_56_eq), .lt(comparator_56_lt));  // open: gt
  // OR_Gate _0_2 has open pins: in0=_0_out, in1=and_18_out, in2=or_9_out, in3=or_6_out, in4=or_2_out, out=open
  or u__1_2 (_1_2_out, or_25_out, and_19_out, or_12_out, or_4_out, or_1_out);
  or u__2_2 (_2_2_out, or_26_out, comparator_24_gt, and_20_out, comparator_12_gt, comparator_4_gt);
  or u__3_2 (_3_2_out, or_27_out, and_21_out, comparator_21_lt, comparator_9_lt, comparator_1_lt);
  and and_44 (and_44_out, comparator_44_gt, comparator_45_lt);
  and and_45 (and_45_out, comparator_46_gt, comparator_47_lt);
  and and_46 (and_46_out, comparator_48_gt, comparator_49_lt);
  and and_47 (and_47_out, comparator_51_gt, comparator_52_lt);
  and and_48 (and_48_out, comparator_53_gt, comparator_54_lt);
  and and_49 (and_49_out, comparator_55_gt, comparator_56_lt);
  or _1_3 (_1_3_out, comparator_44_eq, and_44_out, comparator_45_eq);
  or _2_3 (_2_3_out, comparator_46_eq, and_45_out, comparator_47_eq);
  or _3_3 (_3_3_out, comparator_48_eq, and_46_out, comparator_49_eq);
  or _1_4 (_1_4_out, comparator_51_eq, and_47_out, comparator_52_eq);
  or _2_4 (_2_4_out, comparator_53_eq, and_48_out, comparator_54_eq);
  or _3_4 (_3_4_out, comparator_55_eq, and_49_out, comparator_56_eq);
  // AND_Gate and_50 is placed but not wired
  and _1_5 (_1_5_out, _1_3_out, _1_2_out);
  and _2_5 (_2_5_out, _2_3_out, _2_2_out);
  and _3_5 (_3_5_out, _3_3_out, _3_2_out);
  and _1_6 (_1_6_out, _1_4_out, _1_out);
  and _2_6 (_2_6_out, _2_4_out, _2_out);
  and _3_6 (_3_6_out, _3_4_out, _3_out);
  Priority_Encoder #(.select(2)) priority_encoder_9 (
    .in0(comparator_43_eq), .in1(_1_5_out), .in2(_2_5_out), .in3(_3_5_out), .out(out_88));  // open: gs, en_out, en_in
  Priority_Encoder #(.select(2)) priority_encoder_10 (
    .in0(comparator_50_eq), .in1(_1_6_out), .in2(_2_6_out), .in3(_3_6_out), .out(out_93));  // open: gs, en_out, en_in
  assign out_89 = {{2{1'b0}}, out_88};  // Bit_Extender bit_extender_9

  // Notes on the sheet:
  //   60
  //   80
  //   81
  //   100
  //   Heart Rate Module
  //   Below 60 detector
  //   40
  //   60
  //   61
  //   90
  //   5
  //   15
  //   16
  //   20
  //   Speed Classifier Module
  //   Blood Vessel Thickness Module
  //   Blood vessel size to be entered in the binary concverted form of 10^-4 m for simplicity of the device
  //   93
  //   94
  //   100
  //   120
  //   93
  //   94
  //   100
  //   120
  //   3
  //   2
  //   12
  //   15
  //   16
  //   20
  //   Side Proximity sensor module(Left)
  //   Side Proximity sensr module (Right)
  //   0
  //   1
  //   Blink Rate Module
  //   Front Proximity Sensor Module
  //   10
  //   30
  //   31
  //   120
  //   121
  //   180
  //   3
  //   2
  //   Below 40 kmph
  //   61 to 90 kmph
  //   Above 90 kmph
  //   0
  //   41 to 60 kmph
  //   Steering Angle change Monitor
  //   3
  //   12
  //   15
  //   16
  //   20
  //   0
  //   1
  //   2
  //   Overspeed Seveity Detection Module
  //   3
  //   2
  //   1
  //   1
  //   0
  //   22
  //   45
  //   88
  //   120
  //   121 to 180 degrees
  //   Above 360 degrees
  //   0
  //   3
  //   Distance proximity Module
  //   3
  //   2
  //   1
  //   0
  //   1
  //   2
  //   13
  //   23
  //   24
  //   35
  //   11 To 30 degrees
  //   31 to 120 degrees
  //   Perspiration Module
  //   0
  //   1
  //   2
  //   3
  //   0 to 10 degrees
  //   Below 40 kmph
  //   41 to 60 kmph
  //   61 to 90 kmph
  //   Above 90 kmph
  //   2
  //   3
  //   0
  //   1
  //   0
  //   0
  //   0
  //   0
  //   0
  //   1
  //   2
  //   3
  //   0
  //   1
  //   2
  //   3
  //   0
  //   1
  //   3
  //   3
  //   1
  //   2
  //   3
  //   3
  //   0
  //   1
  //   2
  //   3
  //   Low  Priority Module
endmodule
